# Fritzing sketch Absensi Digital (RFID) (saved by Fritzing 0.9.4)

parts:
  U1 = ESP8266 NodeMCU LoLin module
  Part1 = RFID-RC522 [part_number=101218]
  LCM1602_IIC1 = LCM1602 IIC [part_number="LCM1602 IIC" chip_label="LCM1602 IIC" package="DIP (Dual Inline) [THT]"]
  LED1 = smd LED [color="Red (633nm)" package="0603 [SMD]"]
  J1 = Piezo Speaker
  VCC1 = Battery
  LED2 = smd LED [color="Red (633nm)" package="0603 [SMD]"]
  U2 = SWITCH_SPDT [package=kps-1290]
  LCD1 = LCD screen

nets:
  N1: U1.D0, Part1.RST
  N2: U1.D1, LCM1602_IIC1.SCL
  N3: U1.D2, LCM1602_IIC1.SDA
  N4: U1.D3, LED1.anode
  N5: U1.D4, Part1.SDA
  3V3: U1.3V3, Part1.3.3V
  GND: U1.GND, Part1.GND, LCM1602_IIC1.GND, LED1.cathode, J1.pin1, LED2.cathode, U2.O
  N6: U1.D5, Part1.SCK
  N7: U1.D6, Part1.MISO
  N8: U1.D7, Part1.MOSI
  N9: U1.D8, J1.pin2, LED2.anode
  VIN: U1.Vin, LCM1602_IIC1.VCC, VCC1.+
  VSS: LCM1602_IIC1.VSS, LCD1.VSS
  VDD: LCM1602_IIC1.VDD, LCD1.VDD
  N10: LCM1602_IIC1.V0, LCD1.V0
  N11: LCM1602_IIC1.RS, LCD1.RS
  N12: LCM1602_IIC1.RW, LCD1.R/W
  N13: LCM1602_IIC1.E, LCD1.E
  N14: LCM1602_IIC1.D0, LCD1.DB0
  N15: LCM1602_IIC1.D1, LCD1.DB1
  N16: LCM1602_IIC1.D2, LCD1.DB2
  N17: LCM1602_IIC1.D3, LCD1.DB3
  N18: LCM1602_IIC1.D4, LCD1.DB4
  N19: LCM1602_IIC1.D5, LCD1.DB5
  N20: LCM1602_IIC1.D6, LCD1.DB6
  N21: LCM1602_IIC1.D7, LCD1.DB7
  N22: LCM1602_IIC1.A, LCD1.LED+
  N23: LCM1602_IIC1.K, LCD1.LED-
  N24: LCM1602_IIC1.LED_A, LCM1602_IIC1.LED_B
  N25: VCC1.-, U2.P

notes:
  NodeMCU 40.000
  LCD 16x2 + I2C 30.000
  RFID RC522 25.000
  LED 1.000
  Buzzer 1.000
  Baterai / Adaptor 25.000
  Lain-lain
  (PCB, Jumper, Solder,
  Pin Header, dsb) 20.000
  Total Harga 142.000
  (Belum termasuk biaya pengiriman)
  NodeMCU > Adaptor/Battery
  VIN > VCC (5V)
  GND > GND
  I2C LCD 16x2 > Adaptor/Battery
  VCC > VCC (5V)
  GND > GND + GND (NodeMCU)
  I2C LCD 16x2 > NodeMCU
  SDA > D2
  SCL > D1
  RFID RC522 > NodeMCU
  3.3V > 3V
  RST > D0
  GND > GND
  MISO > D6
  MOSI > D7
  SCK > D5
  SDA > D4
  LED MERAH + BUZZER > NodeMCU
  VCC > D8
  GND > GND
  LED HIJAU > NodeMCU
  VCC > D3
  GND > GND

custom parts:
  ESP8266 NodeMCU LoLin module: ESP8266 based NodeMCU
  LCM1602 IIC: I2C-Module to use a 1602 or 2004 LCD on with the wire.h libory Serial LCD Modul
